# Fritzing sketch SmartHouseplant_Fritzing (saved by Fritzing 1.0.0rc)
breadboards: 1

parts:
  A1 = Particle - Photon2
  Chirp!_Soil_Moisture_Sensor1 = Chirp! Soil Moisture Sensor v2.7.3
  Q2 = PNP-Transistor [package="TO92 [THT]"]
  R1 = Resistor [tolerance=±5% power=0.25W resistance=220 package=THT]
  R2 = Resistor [tolerance=±5% power=0.25W resistance=220 package=THT]

nets:
  N1: A1.Pin_4, A1.Pin_30, Q2.C, R1.Pin_0
  N2: A1.Pin_7, Chirp!_Soil_Moisture_Sensor1.pin_4
  N3: A1.Pin_11, Chirp!_Soil_Moisture_Sensor1.pin_2
  N4: A1.Pin_12, Q2.B, R1.Pin_1
  N5: A1.Pin_13, Chirp!_Soil_Moisture_Sensor1.Pin_0
  N6: Q2.E, R2.Pin_1

custom parts:
  Particle - Photon2: The Photon 2 is a microcontroller and Wi-Fi networking developed by particle. Features: 802.11a/b/g/n Wi-Fi, 2.4 GHz and 5 GHz Integrated PCB antenna Integrated U.FL connector for external antenna Integrated RF switch BLE 5 using same antenna as Wi-Fi Realtek RTL8721DM MCU ARM Cortex M33 CPU, 200 MHz 2048 KB (2 MB) user application maximum size 3072 KB (3 MB) of RAM available to user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
